// Digital circuit 2-bit multiplier.dig as structural Verilog
module _2_bit_multiplier (
  input  A0,
  input  A1,
  input  B0,
  input  B1,
  output P0,
  output P1,
  output P2,
  output P3,
  output [3:0] Product
);

  wire and_2_out, and_3_out, and_4_out, and_5_out;

  and and_1 (P0, A0, B0);
  and and_2 (and_2_out, A1, B0);
  and and_3 (and_3_out, A0, B1);
  and and_4 (and_4_out, A1, B1);
  xor xor_1 (P1, and_2_out, and_3_out);
  and and_5 (and_5_out, and_2_out, and_3_out);
  xor xor_2 (P2, and_5_out, and_4_out);
  and and_6 (P3, and_5_out, and_4_out);

  assign Product = {P3, P2, P1, P0};
endmodule
