// Digital circuit GPR.dig as structural Verilog
module GPR (
  input  [1:0] Address,
  input  [1:0] CTRL__Load__Store__Clear,
  input  [3:0] Input,
  input  clk,
  output [3:0] Output
);

  wire and_1_out, and_2_out, and_3_out, and_4_out, decoder_1_out_0, decoder_1_out_1, decoder_1_out_2,
       decoder_1_out_3;
  wire [3:0] R0_output, R1_output, R2_output, R3_output;

  Decoder #(.Selector_Bits(2)) decoder_1 (
    .sel(Address), .out_0(decoder_1_out_0), .out_1(decoder_1_out_1), .out_2(decoder_1_out_2),
    .out_3(decoder_1_out_3));
  and and_1 (and_1_out, clk, decoder_1_out_0);
  and and_2 (and_2_out, clk, decoder_1_out_1);
  and and_3 (and_3_out, clk, decoder_1_out_2);
  and and_4 (and_4_out, clk, decoder_1_out_3);
  _4_bit_register R0 (
    .Input(Input), .CTRL__Load__Store__Clear(CTRL__Load__Store__Clear), .clk(and_1_out), .Output(R0_output));
  _4_bit_register R1 (
    .Input(Input), .CTRL__Load__Store__Clear(CTRL__Load__Store__Clear), .clk(and_2_out), .Output(R1_output));
  _4_bit_register R2 (
    .Input(Input), .CTRL__Load__Store__Clear(CTRL__Load__Store__Clear), .clk(and_3_out), .Output(R2_output));
  _4_bit_register R3 (
    .Input(Input), .CTRL__Load__Store__Clear(CTRL__Load__Store__Clear), .clk(and_4_out), .Output(R3_output));
  Multiplexer #(.Selector_Bits(2), .Bits(4)) multiplexer_1 (
    .sel(Address), .in_0(R0_output), .in_1(R1_output), .in_2(R2_output), .in_3(R3_output), .out(Output));

  // Notes on the sheet:
  //   clk: Hz: 100
endmodule
