// Digital circuit IR.dig as structural Verilog
module IR (
  input  [3:0] Input,
  input  CTRL__Load__Store,
  input  [1:0] CTRL__Load__Store__Clear,
  input  clk,
  output [3:0] Output
);

  wire [3:0] multiplexer_1_out;

  Multiplexer #(.Bits(4)) multiplexer_1 (.sel(CTRL__Load__Store), .in_0(Output), .in_1(Input), .out(multiplexer_1_out));
  _4_bit_register _4_bit_register_1 (
    .Input(multiplexer_1_out), .CTRL__Load__Store__Clear(CTRL__Load__Store__Clear), .clk(clk), .Output(Output));

  // Notes on the sheet:
  //   clk: Hz: 100
endmodule
