// Digital circuit Registers_DRAM.dig as structural Verilog
module Registers_DRAM (
  input  [1:0] Address,
  input  [3:0] Input,
  input  clk,
  input  [1:0] CTRL_GPR,
  input  GPR_SelectInput,
  input  [1:0] CTRL_Memory,
  input  Memory_SelectChip,
  input  [1:0] CTRL_IR,
  input  [1:0] CTRL_PC,
  input  [3:0] Load_Manual_PC,
  output [3:0] Output
);

  wire [3:0] gpr_1_output, memory_1_output, multiplexer_1_out, pc_1_output;

  Multiplexer #(.Bits(4)) multiplexer_1 (
    .sel(GPR_SelectInput), .in_0(Input), .in_1(memory_1_output), .out(multiplexer_1_out));
  GPR gpr_1 (
    .Address(Address), .CTRL__Load__Store__Clear(CTRL_GPR), .Input(multiplexer_1_out), .clk(clk),
    .Output(gpr_1_output));
  PC pc_1 (.CTRL__Load__Increment__Reset(CTRL_PC), .clk(clk), .Manual_Load(Load_Manual_PC), .Output(pc_1_output));
  memory memory_1 (
    .Address(pc_1_output), .clk(clk), .Input(gpr_1_output), .CTRL__Read__Write__Reset(CTRL_Memory),
    .Select_Chip(Memory_SelectChip), .Output(memory_1_output));
  IR ir_1 (.Input(memory_1_output), .CTRL__Load__Store(CTRL_IR), .clk(clk), .Output(Output));
endmodule
