// Digital circuit memory.dig as structural Verilog
module memory (
  input  [3:0] Address,
  input  Clock,
  input  [3:0] Input,
  input  [1:0] CTRL__Read__Write__Reset,
  input  Chip_Select,
  output [3:0] Output
);

  wire demultiplexer_1_out_0, demultiplexer_1_out_1, demultiplexer_1_out_2, demultiplexer_1_out_3,
       demultiplexer_1_out_4, demultiplexer_1_out_5, demultiplexer_1_out_6, demultiplexer_1_out_7,
       demultiplexer_1_out_8, demultiplexer_1_out_9, demultiplexer_1_out_10, demultiplexer_1_out_11,
       demultiplexer_1_out_12, demultiplexer_1_out_13, demultiplexer_1_out_14, demultiplexer_1_out_15;
  wire [3:0] driver_1_out, multiplexer_1_out, R0_output, R1_output, R2_output, R3_output, R4_output,
       R5_output, R6_output, R7_output, R8_output, R9_output, R10_output, R11_output, R12_output, R13_output,
       R14_output, R15_output;

  assign driver_1_out = Chip_Select ? Input : 4'bz;  // Driver driver_1
  Demultiplexer #(.Selector_Bits(4)) demultiplexer_1 (
    .sel(Address), .in(Clock), .out_0(demultiplexer_1_out_0), .out_1(demultiplexer_1_out_1),
    .out_2(demultiplexer_1_out_2), .out_3(demultiplexer_1_out_3), .out_4(demultiplexer_1_out_4),
    .out_5(demultiplexer_1_out_5), .out_6(demultiplexer_1_out_6), .out_7(demultiplexer_1_out_7),
    .out_8(demultiplexer_1_out_8), .out_9(demultiplexer_1_out_9), .out_10(demultiplexer_1_out_10),
    .out_11(demultiplexer_1_out_11), .out_12(demultiplexer_1_out_12), .out_13(demultiplexer_1_out_13),
    .out_14(demultiplexer_1_out_14), .out_15(demultiplexer_1_out_15));
  _4_bit_register R0 (
    .Input(driver_1_out), .CTRL__Load__Store__Clear(CTRL__Read__Write__Reset), .clk(demultiplexer_1_out_0),
    .Output(R0_output));
  _4_bit_register R4 (
    .Input(driver_1_out), .CTRL__Load__Store__Clear(CTRL__Read__Write__Reset), .clk(demultiplexer_1_out_4),
    .Output(R4_output));
  _4_bit_register R8 (
    .Input(driver_1_out), .CTRL__Load__Store__Clear(CTRL__Read__Write__Reset), .clk(demultiplexer_1_out_8),
    .Output(R8_output));
  _4_bit_register R12 (
    .Input(driver_1_out), .CTRL__Load__Store__Clear(CTRL__Read__Write__Reset), .clk(demultiplexer_1_out_12),
    .Output(R12_output));
  _4_bit_register R1 (
    .Input(driver_1_out), .CTRL__Load__Store__Clear(CTRL__Read__Write__Reset), .clk(demultiplexer_1_out_1),
    .Output(R1_output));
  _4_bit_register R5 (
    .Input(driver_1_out), .CTRL__Load__Store__Clear(CTRL__Read__Write__Reset), .clk(demultiplexer_1_out_5),
    .Output(R5_output));
  _4_bit_register R9 (
    .Input(driver_1_out), .CTRL__Load__Store__Clear(CTRL__Read__Write__Reset), .clk(demultiplexer_1_out_9),
    .Output(R9_output));
  _4_bit_register R13 (
    .Input(driver_1_out), .CTRL__Load__Store__Clear(CTRL__Read__Write__Reset), .clk(demultiplexer_1_out_13),
    .Output(R13_output));
  _4_bit_register R2 (
    .Input(driver_1_out), .CTRL__Load__Store__Clear(CTRL__Read__Write__Reset), .clk(demultiplexer_1_out_2),
    .Output(R2_output));
  _4_bit_register R6 (
    .Input(driver_1_out), .CTRL__Load__Store__Clear(CTRL__Read__Write__Reset), .clk(demultiplexer_1_out_6),
    .Output(R6_output));
  _4_bit_register R10 (
    .Input(driver_1_out), .CTRL__Load__Store__Clear(CTRL__Read__Write__Reset), .clk(demultiplexer_1_out_10),
    .Output(R10_output));
  _4_bit_register R14 (
    .Input(driver_1_out), .CTRL__Load__Store__Clear(CTRL__Read__Write__Reset), .clk(demultiplexer_1_out_14),
    .Output(R14_output));
  _4_bit_register R3 (
    .Input(driver_1_out), .CTRL__Load__Store__Clear(CTRL__Read__Write__Reset), .clk(demultiplexer_1_out_3),
    .Output(R3_output));
  _4_bit_register R7 (
    .Input(driver_1_out), .CTRL__Load__Store__Clear(CTRL__Read__Write__Reset), .clk(demultiplexer_1_out_7),
    .Output(R7_output));
  _4_bit_register R11 (
    .Input(driver_1_out), .CTRL__Load__Store__Clear(CTRL__Read__Write__Reset), .clk(demultiplexer_1_out_11),
    .Output(R11_output));
  _4_bit_register R15 (
    .Input(driver_1_out), .CTRL__Load__Store__Clear(CTRL__Read__Write__Reset), .clk(demultiplexer_1_out_15),
    .Output(R15_output));
  Multiplexer #(.Selector_Bits(4), .Bits(4)) multiplexer_1 (
    .sel(Address), .in_0(R0_output), .in_1(R1_output), .in_2(R2_output), .in_3(R3_output), .in_4(R4_output),
    .in_5(R5_output), .in_6(R6_output), .in_7(R7_output), .in_8(R8_output), .in_9(R9_output),
    .in_10(R10_output), .in_11(R11_output), .in_12(R12_output), .in_13(R13_output), .in_14(R14_output),
    .in_15(R15_output), .out(multiplexer_1_out));
  assign Output = Chip_Select ? multiplexer_1_out : 4'bz;  // Driver driver_2
endmodule
