// Digital circuit RegisterFile_ALU.dig as structural Verilog
module RegisterFile_ALU (
  input  clk,
  input  [7:0] ctrl_registers,
  input  [1:0] Select_data,
  input  [3:0] Write_data,
  input  [1:0] Select_read1,
  input  [1:0] Select_read2,
  input  [2:0] S1_S0_C_in,
  output [3:0] Output,
  output Overflow
);

  wire [3:0] register_file_1_read_data_1, register_file_1_read_data_2;

  Register_file register_file_1 (
    .clk(clk), .Write_data(Write_data), .Select_data(Select_data), .ctrl_registers(ctrl_registers),
    .Select_read1(Select_read1), .Select_read2(Select_read2), .Read_data_1(register_file_1_read_data_1),
    .Read_data_2(register_file_1_read_data_2));
  ALU alu_1 (
    .S_1_S_0_C_in(S1_S0_C_in), .B(register_file_1_read_data_2), .A(register_file_1_read_data_1), .D(Output),
    .Overflow(Overflow));
endmodule
