// Digital circuit 4-D-Flipflops.dig as structural Verilog
module _4_D_Flipflops (
  input  [3:0] Input,
  input  clk,
  output [3:0] Output
);

  D_FF d_ff_1 (.D(Input[3]), .C(clk), .Q(Output[3]));  // open: nQ
  D_FF d_ff_2 (.D(Input[2]), .C(clk), .Q(Output[2]));  // open: nQ
  D_FF d_ff_3 (.D(Input[1]), .C(clk), .Q(Output[1]));  // open: nQ
  D_FF d_ff_4 (.D(Input[0]), .C(clk), .Q(Output[0]));  // open: nQ
endmodule
