// Digital circuit Register-file.dig as structural Verilog
module Register_file (
  input  clk,
  input  [3:0] Write_data,
  input  [1:0] Select_write,
  input  [7:0] ctrl_registers,
  input  [1:0] Select_read1,
  input  [1:0] Select_read2,
  output [3:0] Read_data_1,
  output [3:0] Read_data_2
);

  wire [3:0] _4_bit_register_1_output, _4_bit_register_2_output, _4_bit_register_3_output,
       _4_bit_register_4_output, demultiplexer_1_out_0, demultiplexer_1_out_1, demultiplexer_1_out_2,
       demultiplexer_1_out_3;

  Demultiplexer #(.Selector_Bits(2), .Bits(4)) demultiplexer_1 (
    .sel(Select_write), .in(Write_data), .out_0(demultiplexer_1_out_0), .out_1(demultiplexer_1_out_1),
    .out_2(demultiplexer_1_out_2), .out_3(demultiplexer_1_out_3));
  _4_bit_register _4_bit_register_1 (
    .Input(demultiplexer_1_out_0), .CTRL__Load__Store__Clear(ctrl_registers[1:0]), .clk(clk),
    .Output(_4_bit_register_1_output));
  _4_bit_register _4_bit_register_2 (
    .Input(demultiplexer_1_out_1), .CTRL__Load__Store__Clear(ctrl_registers[3:2]), .clk(clk),
    .Output(_4_bit_register_2_output));
  _4_bit_register _4_bit_register_3 (
    .Input(demultiplexer_1_out_2), .CTRL__Load__Store__Clear(ctrl_registers[5:4]), .clk(clk),
    .Output(_4_bit_register_3_output));
  _4_bit_register _4_bit_register_4 (
    .Input(demultiplexer_1_out_3), .CTRL__Load__Store__Clear(ctrl_registers[7:6]), .clk(clk),
    .Output(_4_bit_register_4_output));
  Multiplexer #(.Selector_Bits(2), .Bits(4)) multiplexer_1 (
    .sel(Select_read1), .in_0(_4_bit_register_1_output), .in_1(_4_bit_register_2_output),
    .in_2(_4_bit_register_3_output), .in_3(_4_bit_register_4_output), .out(Read_data_1));
  Multiplexer #(.Selector_Bits(2), .Bits(4)) multiplexer_2 (
    .sel(Select_read2), .in_0(_4_bit_register_1_output), .in_1(_4_bit_register_2_output),
    .in_2(_4_bit_register_3_output), .in_3(_4_bit_register_4_output), .out(Read_data_2));
endmodule
