// Digital circuit Problem 7.dig as structural Verilog
module Problem_7 (
  input  I,
  input  clk,
  output X
);

  wire and_1_out, and_2_out, S0_q, S1_nq, S1_q;

  and and_1 (and_1_out, S1_nq, S0_q);
  and and_2 (and_2_out, S1_q, I, S0_q);
  D_FF S1 (.D(and_1_out), .C(clk), .Q(S1_q), .nQ(S1_nq));
  D_FF S0 (.D(and_2_out), .C(clk), .Q(S0_q));  // open: nQ
  or or_1 (X, S1_nq, S0_q);

  // Notes on the sheet:
  //   clk: Hz: 200
endmodule
