// Digital circuit Problem 9 (110 Sequence Detector).dig as structural Verilog
module Problem_9__110_Sequence_Detector (
  input  Input,
  input  clk,
  output Output
);

  wire and_1_out, and_2_out, and_3_out, and_4_out, and_5_out, D0_nq, D0_q, D1_nq, D1_q, not_1_out, or_1_out,
       or_2_out;

  not not_1 (not_1_out, Input);
  and and_1 (and_1_out, D0_q, Input, D1_nq);
  and and_2 (and_2_out, D1_q, D0_nq);
  and and_3 (and_3_out, D1_nq, Input, D0_nq);
  and and_4 (and_4_out, D1_q, Input, D0_q);
  and and_5 (and_5_out, D1_q, not_1_out, D0_nq);
  or or_1 (or_1_out, and_1_out, and_2_out);
  or or_2 (or_2_out, and_3_out, and_4_out, and_5_out);
  D_FF D1 (.D(or_1_out), .C(clk), .Q(D1_q), .nQ(D1_nq));
  D_FF D0 (.D(or_2_out), .C(clk), .Q(D0_q), .nQ(D0_nq));
  and and_6 (Output, D1_q, D0_q);

  // Notes on the sheet:
  //   clk: Hz: 200
endmodule
