// Digital circuit intr-mem-module.dig as structural Verilog
module intr_mem_module (
  input  clk,
  input  [1:0] IR_ctrl,
  input  [1:0] pc_ctrl,
  input  [3:0] instr_mem_input,
  input  [1:0] intr_mem_ctrl,
  output [3:0] pc_output,
  output [15:0] ir_output,
  output ALU_enable
);

  wire not_1_out, not_2_out;
  wire [1:0] demultiplexer_1_out_0, demultiplexer_1_out_1, demultiplexer_1_out_2, demultiplexer_1_out_3;
  wire [3:0] demultiplexer_2_out_0, demultiplexer_2_out_1, demultiplexer_2_out_2, demultiplexer_2_out_3,
       IR0_output, IR1_output, IR2_output, IR3_output, memory_1_output;

  _4_bit_ProgramCounter _4_bit_programcounter_1 (.CTRL(pc_ctrl), .clk(clk), .Output(pc_output));
  memory memory_1 (
    .Address(pc_output), .CTRL(intr_mem_ctrl), .Input(instr_mem_input), .clk(clk), .Output(memory_1_output));
  Demultiplexer #(.Selector_Bits(2), .Bits(2)) demultiplexer_1 (
    .sel(pc_output[1:0]), .in(IR_ctrl), .out_0(demultiplexer_1_out_0), .out_1(demultiplexer_1_out_1),
    .out_2(demultiplexer_1_out_2), .out_3(demultiplexer_1_out_3));
  Demultiplexer #(.Selector_Bits(2), .Bits(4)) demultiplexer_2 (
    .sel(pc_output[1:0]), .in(memory_1_output), .out_0(demultiplexer_2_out_0), .out_1(demultiplexer_2_out_1),
    .out_2(demultiplexer_2_out_2), .out_3(demultiplexer_2_out_3));
  _4_bit_InstructionRegister IR0 (
    .Input(demultiplexer_2_out_0), .CTRL(demultiplexer_1_out_0), .clk(clk), .Output(IR0_output));
  _4_bit_InstructionRegister IR1 (
    .Input(demultiplexer_2_out_1), .CTRL(demultiplexer_1_out_1), .clk(clk), .Output(IR1_output));
  _4_bit_InstructionRegister IR2 (
    .Input(demultiplexer_2_out_2), .CTRL(demultiplexer_1_out_2), .clk(clk), .Output(IR2_output));
  _4_bit_InstructionRegister IR3 (
    .Input(demultiplexer_2_out_3), .CTRL(demultiplexer_1_out_3), .clk(clk), .Output(IR3_output));
  not not_1 (not_1_out, pc_output[0]);
  not not_2 (not_2_out, pc_output[1]);
  and and_1 (ALU_enable, not_1_out, not_2_out);
  assign ir_output = ALU_enable ? {IR3_output, IR2_output, IR1_output, IR0_output} : 16'bz;  // Driver driver_1
endmodule
